// Logisim project hc01.circ as structural Verilog: 5 circuits, main circuit NotGate
module NotGate (
  input  a,
  output nota
);

  nand nand_1 (nota, a, a);
endmodule

module AndGate (
  input  a,
  input  b,
  output aandb
);

  wire nand_1_out;

  nand nand_1 (nand_1_out, a, b);
  NotGate notgate_1 (.nota(aandb), .a(nand_1_out));
endmodule

module OrGate (
  input  a,
  input  b,
  output aorb
);

  wire notgate_1_nota, notgate_2_nota;

  NotGate notgate_1 (.nota(notgate_1_nota), .a(a));
  NotGate notgate_2 (.nota(notgate_2_nota), .a(b));
  nand nand_1 (aorb, notgate_1_nota, notgate_2_nota);
endmodule

module XorGate (
  input  a,
  input  b,
  output axorb
);

  wire andgate_1_aandb, andgate_2_aandb, notgate_1_nota, notgate_2_nota;

  NotGate notgate_1 (.nota(notgate_1_nota), .a(a));
  NotGate notgate_2 (.nota(notgate_2_nota), .a(b));
  AndGate andgate_1 (.aandb(andgate_1_aandb), .b(b), .a(notgate_1_nota));
  AndGate andgate_2 (.aandb(andgate_2_aandb), .b(notgate_2_nota), .a(a));
  OrGate orgate_1 (.aorb(axorb), .a(andgate_1_aandb), .b(andgate_2_aandb));
endmodule

module MuxGate (
  input  a,
  input  sel,
  input  b,
  output muxab
);

  wire andgate_1_aandb, andgate_2_aandb, notgate_1_nota;

  NotGate notgate_1 (.nota(notgate_1_nota), .a(sel));
  AndGate andgate_1 (.aandb(andgate_1_aandb), .b(notgate_1_nota), .a(a));
  AndGate andgate_2 (.aandb(andgate_2_aandb), .b(b), .a(sel));
  OrGate orgate_1 (.aorb(muxab), .a(andgate_1_aandb), .b(andgate_2_aandb));
endmodule
